# Fritzing sketch flipper_clone (saved by Fritzing 0.9.3b)
breadboards: 2

parts:
  Pico_H1 = Raspberry Pi Pico H
  OLED1 = OLED 128x64 I2C Monochrome Display
  S1 = Pushbutton [package="[THT]"]
  S2 = Pushbutton [package="[THT]"]
  S3 = Pushbutton [package="[THT]"]
  S4 = Pushbutton [package="[THT]"]
  Part1 = PN532 Elechouse RFID NFC Module V3
  IR1 = tl1838 [package=THT]
  U1 = ESP8266 WiFi Module [part_number=ESP8266]
  D1 = LTE-302 [package=lte-302]
  YwRobot_Power_Supply1 = YwRobot Breadboard Power Supply [part_number=545043]
  Part2 = Real Time Clock Module - DS1307 RTC Breakout Board  # not connected

nets:
  GND: Pico_H1.GND, OLED1.GND, Part1.GND, IR1.GND, U1.GND, D1.C, YwRobot_Power_Supply1.GND#11
  N1: Pico_H1.GP28_A2, D1.A
  N2: Pico_H1.GP22, IR1.OUT
  N3: Pico_H1.GP17, U1.TXD
  N4: Pico_H1.GP16, U1.RXD
  N5: Pico_H1.GP5, Part1.SDA
  N6: Pico_H1.GP4, Part1.SCL
  N7: Pico_H1.GP1, OLED1.SCK
  N8: Pico_H1.GP0, OLED1.SDA
  VCC: OLED1.VDD, Part1.VCC, IR1.VCC, U1.VCC, U1.RST, YwRobot_Power_Supply1.VCC#5
  N9: S1.Pin_1, S1.Pin_2
  N10: S1.Pin_3, S1.Pin_4
  N11: S2.Pin_1, S2.Pin_2
  N12: S2.Pin_3, S2.Pin_4
  N13: S3.Pin_1, S3.Pin_2
  N14: S3.Pin_3, S3.Pin_4
  N15: S4.Pin_1, S4.Pin_2
  N16: S4.Pin_3, S4.Pin_4

custom parts:
  Raspberry Pi Pico H: Raspberry Pi Pico H. Based around the RP2040 microcontroller the Pico H is a low cost microcontroller device bringing Raspberry Pi quality, cost, and easy of use to the microcontroller space.
  PN532 Elechouse RFID NFC Module V3: NFC is a popular technology in recent years. We often heard this work while smart phone company such as Samsung or HTC introduces their latest high-end phones. Almost all the high-end phone in the market support NFC. Near field communication (NFC) is a set of standards for smart phones and similar devices to establish radio communication with each other by touching them together or bringing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
  tl1838: The TL1838 is a miniaturized receiver for infrared remote control systems. A PIN diode and a preamplifier are assembled on a lead frame, the epoxy package acts as an IR filter. The demodulated output signal can be directly decoded by a microprocessor.
  ESP8266 WiFi Module: Generic WiFi Module based on the ESP8266 with onboard PCB antenna and UART communications
  YwRobot Breadboard Power Supply: The YwRobot Breadboard Power Supply (MB-V2) has two power rails; they can be 5V or 3V3. Power to the module can be provided through the female USB socket or through the A10 (female) 2.1mm power jack.
